// Logisim project 4BitAddierer.circ as structural Verilog: 3 circuits, main circuit main
module main (
  input  x4,
  input  y4,
  input  x3,
  input  y3,
  input  x2,
  input  y2,
  input  x1,
  input  y1,
  output s5,
  output s4,
  output s3,
  output s2,
  output s1
);

  wire HA_c, VA_2_c_out, VA_3_c_out;

  VA VA (.x(x4), .y(y4), .c_in(VA_2_c_out), .c_out(s5), .s(s4));
  VA VA_2 (.x(x3), .y(y3), .c_in(VA_3_c_out), .c_out(VA_2_c_out), .s(s3));
  VA VA_3 (.x(x2), .y(y2), .c_in(HA_c), .c_out(VA_3_c_out), .s(s2));
  HA HA (.x(x1), .y(y1), .c(HA_c), .s(s1));
endmodule

module HA (
  input  x,
  input  y,
  output c,
  output s
);

  wire and_2_out, and_3_out, not_1_out, not_2_out;

  and and_1 (c, x, y);
  not not_1 (not_1_out, x);
  and and_2 (and_2_out, not_1_out, y);
  and and_3 (and_3_out, x, not_2_out);
  not not_2 (not_2_out, y);
  or or_1 (s, and_2_out, and_3_out);
endmodule

module VA (
  input  x,
  input  y,
  input  c_in,
  output c_out,
  output s
);

  wire and_1_out, and_2_out, and_3_out, and_4_out, and_5_out, and_6_out, and_7_out, and_8_out, and_9_out,
       and_10_out, not_1_out, not_2_out, not_3_out, not_4_out, not_5_out, not_6_out, not_7_out, not_8_out,
       or_1_out, or_2_out;

  and and_1 (and_1_out, x, y, c_in);
  not not_1 (not_1_out, x);
  and and_2 (and_2_out, not_1_out, y, c_in);
  not not_2 (not_2_out, y);
  and and_3 (and_3_out, x, not_2_out, c_in);
  and and_4 (and_4_out, x, y, not_3_out);
  not not_3 (not_3_out, c_in);
  and and_5 (and_5_out, x, not_4_out);
  not not_4 (not_4_out, y);
  not not_5 (not_5_out, x);
  and and_6 (and_6_out, not_5_out, y);
  and and_7 (and_7_out, x, y);
  not not_6 (not_6_out, x);
  and and_8 (and_8_out, not_6_out, not_7_out);
  not not_7 (not_7_out, y);
  or or_1 (or_1_out, and_5_out, and_6_out);
  not not_8 (not_8_out, c_in);
  or or_2 (or_2_out, and_7_out, and_8_out);
  and and_9 (and_9_out, or_1_out, not_8_out);
  and and_10 (and_10_out, c_in, or_2_out);
  or or_3 (c_out, and_1_out, and_2_out, and_3_out, and_4_out);
  or or_4 (s, and_9_out, and_10_out);
endmodule
