// Logisim project Comperator.circ as structural Verilog: 3 circuits, main circuit main
module main (
  input  a4,
  input  b4,
  input  a3,
  input  b3,
  input  a2,
  input  b2,
  input  a1,
  input  b1,
  input  in_9,
  output out_10
);

  wire comperator_2_out_4, comperator_3_out_4, comperator_4_out_4, konstante_out_2;

  Comperator comperator (.a(a4), .b(b4), .\input (comperator_2_out_4), .out_4(out_10));
  Comperator comperator_2 (.a(a3), .b(b3), .\input (comperator_3_out_4), .out_4(comperator_2_out_4));
  Comperator comperator_3 (.a(a2), .b(b2), .\input (comperator_4_out_4), .out_4(comperator_3_out_4));
  Comperator comperator_4 (.a(a1), .b(b1), .\input (konstante_out_2), .out_4(comperator_4_out_4));
  konst konstante (.in_1(in_9), .out_2(konstante_out_2));
endmodule

module Comperator (
  input  a,
  input  b,
  input  \input ,
  output out_4
);

  wire and_1_out, and_2_out, not_1_out, not_2_out;

  and and_1 (and_1_out, a, b, \input );
  not not_1 (not_1_out, a);
  not not_2 (not_2_out, b);
  and and_2 (and_2_out, not_1_out, not_2_out, \input );
  or or_1 (out_4, and_1_out, and_2_out);
endmodule

module konst (
  input  in_1,
  output out_2
);

  wire and_1_out, and_2_out, not_1_out, not_2_out;

  not not_1 (not_1_out, in_1);
  not not_2 (not_2_out, in_1);
  and and_1 (and_1_out, not_1_out, not_2_out);
  and and_2 (and_2_out, in_1, in_1);
  or or_1 (out_2, and_1_out, and_2_out);
endmodule
