// Logisim project Increase.circ as structural Verilog: 2 circuits, main circuit main
module main (
  input  in_1,
  input  in_2,
  input  in_3,
  input  in_4,
  output out_5,
  output out_6,
  output out_7,
  output out_8
);

  wire ha_2_c, ha_3_c, ha_4_c;

  HA ha_1 (.x(in_1), .y(ha_2_c), .s(out_5));  // open: c
  HA ha_2 (.x(in_2), .y(ha_3_c), .c(ha_2_c), .s(out_6));
  HA ha_3 (.x(in_3), .y(ha_4_c), .c(ha_3_c), .s(out_7));
  HA ha_4 (.x(in_4), .y(1'b1), .c(ha_4_c), .s(out_8));
endmodule

module HA (
  input  x,
  input  y,
  output c,
  output s
);

  wire and_2_out, and_3_out, not_1_out, not_2_out;

  and and_1 (c, x, y);
  not not_1 (not_1_out, x);
  and and_2 (and_2_out, not_1_out, y);
  not not_2 (not_2_out, y);
  and and_3 (and_3_out, x, not_2_out);
  or or_1 (s, and_2_out, and_3_out);
endmodule
