// Logisim project LogisimP1.circ as structural Verilog: 1 circuit, main circuit Wasserbehälter
module \Wasserbehälter  (
  input  X1,
  input  X2,
  input  X3,
  output p1,
  output p2,
  output ab
);

  nand nand_1 (p1, X1, X2, X3);
  nor nor_1 (p2, X1, X2, X3);
  and and_1 (ab, X3, X2);
endmodule
