// Logisim project RS Flip-Flop.circ as structural Verilog: 2 circuits, main circuit main
module main (
  input  s,
  input  r,
  output out_3,
  output out_4
);

  RS_Flip_Flop rs_flip_flop_1 (.s(s), .r(r), .Q(out_3), .minus_Q(out_4));
endmodule

module RS_Flip_Flop (
  input  s,
  input  r,
  output Q,
  output minus_Q
);

  wire and_1_out, not_1_out;

  not not_1 (not_1_out, r);
  or or_1 (Q, s, and_1_out);
  and and_1 (and_1_out, Q, not_1_out);
  not not_2 (minus_Q, Q);
endmodule
